# Fritzing sketch breadboard layout (saved by Fritzing 0.9.3b)
breadboards: 1

parts:
  Part1 = Arduino Uno (Rev3) - ICSP  # not connected
  LED1 = LED - 5mm [color="White (8000K)" package="5 mm [THT]"]
  LED2 = LED - 5mm [color="White (8000K)" package="5 mm [THT]"]
  LED3 = LED - 5mm [color="White (8000K)" package="5 mm [THT]"]
  LED4 = LED - 5mm [color="White (8000K)" package="5 mm [THT]"]
  LED5 = LED - 5mm [color="White (8000K)" package="5 mm [THT]"]
  LED6 = LED - 5mm [color="White (8000K)" package="5 mm [THT]"]
  LED7 = LED - 5mm [color="White (8000K)" package="5 mm [THT]"]  # not connected
  LED8 = LED - 5mm [color="White (8000K)" package="5 mm [THT]"]  # not connected
  LED9 = LED - 5mm [color="White (8000K)" package="5 mm [THT]"]  # not connected

nets:
  N1: LED1.cathode, LED4.cathode
  N2: LED2.cathode, LED5.cathode
  N3: LED3.cathode, LED6.cathode
